# Fritzing sketch data sketch (saved by Fritzing 0.9.3b)

parts:
  Componente1 = Arduino Uno (Rev3)
  U1 = ESP8266 ESP-01 Upgraded WiFi Module [part_number=ESP8266]

nets:
  N1: Componente1.D2, U1.TXD
  N2: Componente1.D3_PWM, U1.RXD
  3V3: Componente1.3V3, U1.VCC, U1.CH_PD
  GND: Componente1.GND, U1.GND

custom parts:
  ESP8266 ESP-01 Upgraded WiFi Module: Upgraded Version ESP-01,all Flash are upgraded to 1M byte.Also support Cloud service remote transmission.
